# Fritzing sketch UEC_SAC_Mod_AC_1S_Rev_1_4 (saved by Fritzing 0.9.0b)
circuit board: 9.9971cm x 10.0015cm
circuit board: 5cm x 5cm
perfboards: 1

parts:
  V+ = female pin header, 1 pin [form="♀ (female)"]
  V- = female pin header, 1 pin [form="♀ (female)"]
  Artesanos_Industriales_del_Sur = female pin header, 1 pin [form="♀ (female)"]
  BY-SA_4 = female pin header, 1 pin [form="♀ (female)"]
  1N4001 = Rectifier Diode [part_number=1N4001 package="300 mil [THT]"]
  100uF = Electrolytic Capacitor [capacitance=100nF voltage=20V package="100 mil [THT, electrolytic]"]
  100uF_2 = Electrolytic Capacitor [capacitance=100nF voltage=20V package="100 mil [THT, electrolytic]"]
  0_1uF = Ceramic Capacitor [capacitance=100nF package="100 mil [THT, multilayer]"]
  10kΩ = Resistor [tolerance=±5% resistance=10k package=THT]
  10kΩ_2 = Resistor [tolerance=±5% resistance=10k package=THT]
  100Ω = Resistor [tolerance=±5% resistance=100 package=THT]
  100Ω_2 = Resistor [tolerance=±5% resistance=100 package=THT]
  SW(+) = male pin header, 2 pins [form="♂ (male)"]
  SW(M) = male pin header, 2 pins [form="♂ (male)"]
  SW(-) = male pin header, 2 pins [form="♂ (male)"]
  330Ω = Resistor [tolerance=±5% resistance=330 package=THT]
  150Ω = Resistor [tolerance=±5% resistance=150 package=THT]
  10kΩ_3 = Resistor [tolerance=±5% resistance=10k package=THT]
  1N4001_2 = Rectifier Diode [part_number=1N4001 package="300 mil [THT]"]
  FUSE = female pin header, 1 pin [form="♀ (female)"]
  ------------------------ = female pin header, 1 pin [form="♀ (female)"]
  +_- = female pin header, 1 pin [form="♀ (female)"]
  V-AC_Out_3 = female pin header, 1 pin [form="♀ (female)"]
  100Ω_3 = Resistor [tolerance=±5% resistance=100 package=THT]
  100Ω_4 = Resistor [tolerance=±5% resistance=100 package=THT]
  10kΩ_4 = Resistor [tolerance=±5% resistance=10k package=THT]
  10kΩ_5 = Resistor [tolerance=±5% resistance=10k package=THT]
  100Ω_5 = Resistor [tolerance=±5% resistance=100 package=THT]
  V-IN = female pin header, 1 pin [form="♀ (female)"]
  V-OUT = female pin header, 1 pin [form="♀ (female)"]
  47Ω_1/2W = Resistor [tolerance=±5% resistance=47 package=THT]
  100Ω_6 = Resistor [tolerance=±5% resistance=100 package=THT]
  ------------------------8 = female pin header, 2 pins [form="♀ (female)"]
  ------------------------7 = female pin header, 2 pins [form="♀ (female)"]
  ------------------------10 = female pin header, 2 pins [form="♀ (female)"]
  ------------------------9 = female pin header, 2 pins [form="♀ (female)"]
  VOUT_PUMP = female pin header, 2 pins [form="♀ (female)"]
  VIN_100-240AC = female pin header, 2 pins [form="♀ (female)"]
  UA+3_3V = Voltage Regulator - 3.3V [package="TO220 [THT]"]
  S_M = female pin header, 2 pins [form="♀ (female)"]
  F_C = female pin header, 2 pins [form="♀ (female)"]
  W_L_T = female pin header, 2 pins [form="♀ (female)"]
  Arduino_Pro_Mini_5V = Arduino Pro Mini v13  # not connected
  2N2222A = NPN-Transistor [package="TO92 [THT]"]
  2N3904 = NPN-Transistor [package="TO92 [THT]"]
  2N2222A_2 = NPN-Transistor [package="TO92 [THT]"]
  0_1uF_2 = Ceramic Capacitor [capacitance=100nF package="100 mil [THT, multilayer]"]
  330Ω_2 = Resistor [tolerance=±5% resistance=330 package=THT]
  330Ω_3 = Resistor [tolerance=±5% resistance=330 package=THT]
  330Ω_4 = Resistor [tolerance=±5% resistance=330 package=THT]
  +BLUE(PUMP) = male pin header, 2 pins [form="♂ (male)"]
  +ORANGE(FC) = male pin header, 2 pins [form="♂ (male)"]
  +RED(TANK) = male pin header, 2 pins [form="♂ (male)"]
  J16 = female pin header, 12 pins [form="♀ (female)"]
  J18 = female pin header, 2 pins [form="♀ (female)"]
  J19 = female pin header, 6 pins [form="♀ (female)"]
  J17 = female pin header, 9 pins [form="♀ (female)"]
  LCD = male pin header, 3 pins [form="♂ (male)"]
  LCD1 = male pin header, 3 pins [form="♂ (male)"]
  10kΩ_6 = Resistor [tolerance=±5% resistance=10k package=THT]
  LCD2 = male pin header, 3 pins [form="♂ (male)"]
  4k7Ω = Resistor [tolerance=±5% resistance=4.7k package=THT]
  LCD3 = male pin header, 3 pins [form="♂ (male)"]
  FUSE_PTC = Resettable Fuse PTC [package=ptc]
  100nF/400V = female pin header, 1 pin [form="♀ (female)"]
  J15 = female pin header, 1 pin [form="♀ (female)"]
  LCD4 = male pin header, 3 pins [form="♂ (male)"]

nets:
  N1: V+.pin1, 1N4001.anode
  N2: V-.pin1, 100uF.-, 100uF_2.-, 0_1uF.1, 10kΩ.Pin_0, 10kΩ_2.Pin_1, 100Ω_2.Pin_0, 10kΩ_3.Pin_1, 100Ω_4.Pin_0, 10kΩ_4.Pin_1, 10kΩ_5.Pin_1, UA+3_3V.GND, 2N3904.E, 0_1uF_2.0, 330Ω_2.Pin_0, 330Ω_3.Pin_0, 330Ω_4.Pin_0, J16.pin9, LCD.pin2, LCD1.pin3, LCD2.pin3, LCD3.pin1, LCD4.pin3
  N3: Artesanos_Industriales_del_Sur.pin1, V-IN.pin1, VIN_100-240AC.pin1, VIN_100-240AC.pin2, J15.pin1
  N4: BY-SA_4.pin1, ------------------------8.pin1, ------------------------8.pin2, ------------------------10.pin1, ------------------------10.pin2
  N5: 1N4001.cathode, FUSE_PTC.1
  N6: 100uF.+, 0_1uF.0, SW(+).pin1, SW(M).pin1, SW(-).pin1, 150Ω.Pin_0, 100Ω_5.Pin_0, 100Ω_6.Pin_1, UA+3_3V.input_voltage, W_L_T.pin2, J17.pin9, LCD.pin3, LCD1.pin2, 10kΩ_6.Pin_0, LCD2.pin2, 4k7Ω.Pin_1, LCD3.pin2, FUSE_PTC.2, LCD4.pin2
  N7: 100uF_2.+, UA+3_3V.output_voltage, 0_1uF_2.1, LCD3.pin3
  N8: 10kΩ.Pin_1, W_L_T.pin1, J16.pin7
  N9: 10kΩ_2.Pin_0, SW(-).pin2, J16.pin3
  N10: 100Ω.Pin_0, 100Ω_3.Pin_0, J16.pin8
  N11: 100Ω.Pin_1, S_M.pin1
  N12: 100Ω_2.Pin_1, 2N2222A_2.E, J17.pin6
  N13: SW(+).pin2, 10kΩ_5.Pin_0, J16.pin1
  N14: SW(M).pin2, 10kΩ_4.Pin_0, J16.pin2
  N15: 330Ω.Pin_0, 10kΩ_3.Pin_0, 2N3904.B
  N16: 330Ω.Pin_1, J17.pin4, LCD4.pin1
  N17: 150Ω.Pin_1, 1N4001_2.cathode, V-AC_Out_3.pin1
  N18: 1N4001_2.anode, +_-.pin1, 2N3904.C
  N19: FUSE.pin1, V-OUT.pin1, 47Ω_1/2W.Pin_1
  N20: ------------------------.pin1, VOUT_PUMP.pin1, VOUT_PUMP.pin2
  N21: 100Ω_3.Pin_1, F_C.pin1
  N22: 100Ω_4.Pin_1, 2N2222A.E, J17.pin5
  N23: 100Ω_5.Pin_1, 2N2222A_2.C
  N24: 47Ω_1/2W.Pin_0, 100nF/400V.pin1
  N25: 100Ω_6.Pin_0, 2N2222A.C
  N26: ------------------------7.pin1, ------------------------7.pin2, ------------------------9.pin1, ------------------------9.pin2
  N27: S_M.pin2, 2N2222A_2.B
  N28: F_C.pin2, 2N2222A.B
  N29: 330Ω_2.Pin_1, +RED(TANK).pin1
  N30: 330Ω_3.Pin_1, +ORANGE(FC).pin1
  N31: 330Ω_4.Pin_1, +BLUE(PUMP).pin1
  N32: +BLUE(PUMP).pin2, J16.pin6
  N33: +ORANGE(FC).pin2, J16.pin5
  N34: +RED(TANK).pin2, J16.pin4
  N35: J16.pin11, J19.pin5
  N36: J16.pin12, J19.pin6
  N37: J18.pin1, J19.pin4
  N38: J18.pin2, J19.pin3
  N39: J19.pin1, J17.pin1
  N40: J19.pin2, J17.pin3
  N41: J17.pin2, LCD.pin1
  N42: J17.pin7, LCD1.pin1, 10kΩ_6.Pin_1
  N43: J17.pin8, LCD2.pin1, 4k7Ω.Pin_0

notes:
  Rx - +
  UEC_Mod. AC-1S Rev. 1.4
  SSR
  Power Supply 100-240VAC->5VDC
  D1 +  -
  D3    +  -
  TXO
  EXTRA SHIELD
  _________________________
  +3.3V
  LCD
  DATA LOGGER
  FLOW +  -
  <---O3--->
  <---O2--->
  <---O1--->
  RF 433MHz
  +
  sacultivo.com
  0 0 0 0 0 0 0
  L     G     N
  Artesanos Industriales del Sur www.aisur.org
  +5V
  GND(-)
  -   -   -
  RXI
  ____________________________________________________________________________________
  Wi-Fi
  ST +  -
  SDA
  SCL
  MISO
  D10
  LEDs
  D + -
