# Fritzing sketch UEC_SAC_Mod_AC_1S_Rev_1_4_1 (copia) (saved by Fritzing 0.9.0b)
circuit board: 9.9971cm x 10.0015cm
perfboards: 1

parts:
  V+ = female pin header, 1 pin [form="♀ (female)"]
  V- = female pin header, 1 pin [form="♀ (female)"]
  Artesanos_Industriales_del_Sur = female pin header, 1 pin [form="♀ (female)"]
  BY-SA_4 = female pin header, 1 pin [form="♀ (female)"]
  100uF = Electrolytic Capacitor [capacitance=100nF voltage=20V package="100 mil [THT, electrolytic]"]
  0_1uF = Ceramic Capacitor [capacitance=100nF package="100 mil [THT, multilayer]"]
  10kΩ = Resistor [tolerance=±5% resistance=10k package=THT]
  10kΩ_2 = Resistor [tolerance=±5% resistance=10k package=THT]
  100Ω = Resistor [tolerance=±5% resistance=100 package=THT]
  100Ω_2 = Resistor [tolerance=±5% resistance=100 package=THT]
  SW(+) = male pin header, 2 pins [form="♂ (male)"]
  SW(M) = male pin header, 2 pins [form="♂ (male)"]
  SW(-) = male pin header, 2 pins [form="♂ (male)"]
  330Ω = Resistor [tolerance=±5% resistance=330 package=THT]
  150Ω = Resistor [tolerance=±5% resistance=150 package=THT]
  10kΩ_3 = Resistor [tolerance=±5% resistance=10k package=THT]
  FUSE = female pin header, 1 pin [form="♀ (female)"]
  ------------------------ = female pin header, 1 pin [form="♀ (female)"]
  +_- = female pin header, 1 pin [form="♀ (female)"]
  V-AC_Out_3 = female pin header, 1 pin [form="♀ (female)"]
  100Ω_3 = Resistor [tolerance=±5% resistance=100 package=THT]
  100Ω_4 = Resistor [tolerance=±5% resistance=100 package=THT]
  10kΩ_4 = Resistor [tolerance=±5% resistance=10k package=THT]
  10kΩ_5 = Resistor [tolerance=±5% resistance=10k package=THT]
  100Ω_5 = Resistor [tolerance=±5% resistance=100 package=THT]
  V-IN = female pin header, 1 pin [form="♀ (female)"]
  V-OUT = female pin header, 1 pin [form="♀ (female)"]
  47Ω_1/2W = Resistor [tolerance=±5% resistance=47 package=THT]
  100Ω_6 = Resistor [tolerance=±5% resistance=100 package=THT]
  ------------------------8 = female pin header, 2 pins [form="♀ (female)"]
  ------------------------7 = female pin header, 2 pins [form="♀ (female)"]
  ------------------------10 = female pin header, 2 pins [form="♀ (female)"]
  ------------------------9 = female pin header, 2 pins [form="♀ (female)"]
  VOUT_PUMP = female pin header, 2 pins [form="♀ (female)"]
  VIN_100-240AC = female pin header, 2 pins [form="♀ (female)"]
  Arduino_Pro_Mini_5V = Arduino Pro Mini v13  # not connected
  2N2222A = NPN-Transistor [package="TO92 [THT]"]
  2N3904 = NPN-Transistor [package="TO92 [THT]"]
  2N2222A_2 = NPN-Transistor [package="TO92 [THT]"]
  330Ω_2 = Resistor [tolerance=±5% resistance=330 package=THT]
  330Ω_3 = Resistor [tolerance=±5% resistance=330 package=THT]
  330Ω_4 = Resistor [tolerance=±5% resistance=330 package=THT]
  +BLUE(PUMP) = male pin header, 2 pins [form="♂ (male)"]
  +ORANGE(FC) = male pin header, 2 pins [form="♂ (male)"]
  +RED(TANK) = male pin header, 2 pins [form="♂ (male)"]
  J16 = female pin header, 12 pins [form="♀ (female)"]
  J18 = female pin header, 2 pins [form="♀ (female)"]
  J17 = female pin header, 9 pins [form="♀ (female)"]
  LCD = male pin header, 3 pins [form="♂ (male)"]
  10kΩ_6 = Resistor [tolerance=±5% resistance=10k package=THT]
  4k7Ω = Resistor [tolerance=±5% resistance=4.7k package=THT]
  FUSE_PTC = Resettable Fuse PTC [package=ptc]
  100nF/400V = female pin header, 1 pin [form="♀ (female)"]
  J15 = female pin header, 1 pin [form="♀ (female)"]
  LCD4 = male pin header, 3 pins [form="♂ (male)"]
  LCD5 = male pin header, 3 pins [form="♂ (male)"]
  LCD6 = male pin header, 3 pins [form="♂ (male)"]
  LCD7 = male pin header, 4 pins [form="♂ (male)"]
  1N4001 = Resistor [tolerance=±5% resistance=47 package=THT]
  1N4002 = Resistor [tolerance=±5% resistance=47 package=THT]
  J20 = female pin header, 2 pins [form="♀ (female)"]
  LCD8 = male pin header, 3 pins [form="♂ (male)"]
  LCD1 = male pin header, 3 pins [form="♂ (male)"]
  LCD2 = male pin header, 3 pins [form="♂ (male)"]
  S_M = female pin header, 2 pins [form="♀ (female)"]
  F_C = female pin header, 2 pins [form="♀ (female)"]
  W_L_T = female pin header, 2 pins [form="♀ (female)"]

nets:
  N1: V+.pin1, 1N4002.Pin_1
  N2: V-.pin1, 100uF.-, 0_1uF.1, 10kΩ.Pin_0, 10kΩ_2.Pin_1, 100Ω_2.Pin_0, 10kΩ_3.Pin_1, 100Ω_4.Pin_0, 10kΩ_4.Pin_1, 10kΩ_5.Pin_1, 2N3904.E, 330Ω_2.Pin_0, 330Ω_3.Pin_0, 330Ω_4.Pin_0, J16.pin9, LCD.pin2, LCD4.pin3, LCD6.pin2, LCD7.pin4, LCD8.pin1, LCD1.pin3, LCD2.pin3
  N3: Artesanos_Industriales_del_Sur.pin1, V-IN.pin1, VIN_100-240AC.pin1, VIN_100-240AC.pin2, 100nF/400V.pin1
  N4: BY-SA_4.pin1, ------------------------8.pin1, ------------------------8.pin2, ------------------------10.pin1, ------------------------10.pin2
  N5: 100uF.+, 0_1uF.0, SW(+).pin1, SW(M).pin1, SW(-).pin1, 150Ω.Pin_0, 100Ω_5.Pin_0, 100Ω_6.Pin_1, J17.pin9, LCD.pin3, 10kΩ_6.Pin_0, 4k7Ω.Pin_1, FUSE_PTC.2, LCD5.pin2, LCD7.pin3, LCD8.pin3, LCD1.pin2, LCD2.pin2, W_L_T.pin2
  N6: 10kΩ.Pin_1, J16.pin7, W_L_T.pin1
  N7: 10kΩ_2.Pin_0, SW(-).pin2, J16.pin3
  N8: 100Ω.Pin_0, 100Ω_3.Pin_0, J16.pin8
  N9: 100Ω.Pin_1, S_M.pin1
  N10: 100Ω_2.Pin_1, 2N2222A_2.E, J17.pin6
  N11: SW(+).pin2, 10kΩ_5.Pin_0, J16.pin1
  N12: SW(M).pin2, 10kΩ_4.Pin_0, J16.pin2
  N13: 330Ω.Pin_0, 10kΩ_3.Pin_0, 2N3904.B
  N14: 330Ω.Pin_1, J17.pin4, LCD4.pin1
  N15: 150Ω.Pin_1, V-AC_Out_3.pin1, 1N4001.Pin_0
  N16: FUSE.pin1, V-OUT.pin1, 47Ω_1/2W.Pin_1
  N17: ------------------------.pin1, VOUT_PUMP.pin1, VOUT_PUMP.pin2
  N18: +_-.pin1, 2N3904.C, 1N4001.Pin_1
  N19: 100Ω_3.Pin_1, F_C.pin1
  N20: 100Ω_4.Pin_1, 2N2222A.E, J17.pin5
  N21: 100Ω_5.Pin_1, 2N2222A_2.C
  N22: 47Ω_1/2W.Pin_0, J15.pin1
  N23: 100Ω_6.Pin_0, 2N2222A.C
  N24: ------------------------7.pin1, ------------------------7.pin2, ------------------------9.pin1, ------------------------9.pin2
  N25: 2N2222A.B, F_C.pin2
  N26: 2N2222A_2.B, S_M.pin2
  N27: 330Ω_2.Pin_1, +RED(TANK).pin1
  N28: 330Ω_3.Pin_1, +ORANGE(FC).pin1
  N29: 330Ω_4.Pin_1, +BLUE(PUMP).pin1
  N30: +BLUE(PUMP).pin2, J16.pin6
  N31: +ORANGE(FC).pin2, J16.pin5
  N32: +RED(TANK).pin2, J16.pin4
  N33: J16.pin11, J20.pin1
  N34: J16.pin12, J20.pin2
  N35: J18.pin1, LCD7.pin2
  N36: J18.pin2, LCD7.pin1
  N37: J17.pin2, LCD.pin1
  N38: J17.pin7, 10kΩ_6.Pin_1, LCD1.pin1
  N39: J17.pin8, 4k7Ω.Pin_0, LCD2.pin1
  N40: FUSE_PTC.1, 1N4002.Pin_0
  N41: LCD4.pin2, LCD5.pin3, LCD6.pin3
  N42: LCD5.pin1, LCD6.pin1

notes:
  Rx - +
  UEC_Mod. AC-1S Rev. 1.4.1
  Power Supply 100-240VAC->5VDC
  D1 +  -
  D3    +  -
  TXO
  EXTRA SHIELD
  _________________________
  +5V
  LCD
  DATA LOGGER
  RF 433MHz
  +
  sacultivo.com
  0 0 0 0 0 0 0
  L     G     N
  Artesanos Industriales del Sur www.aisur.org
  NC
  GND(-)
  -   -   -
  RXI
  ____________________________________________________________________________________
  Wi-Fi
  SCL SDA +  -
  RTC
  LEDs
  - + D
  SSR
  _
  9V
  5V
  OUT  GND  IN
  STEP UP
  ................................
  ................
  REMOTE ACTUATOR
  -
  FLOW +  -
  ST +  -
  CC By-Sa 4.0
  Arduino Pro Mini 5V
  GPS
  GSM
  RF
